// Logisim project CONTADOR SICRONO.circ as structural Verilog: 3 circuits, main circuit main
module main (
  output out_1,
  output out_2,
  output out_3,
  output out_4,
  output out_5
);

  wire CLOCK_out, j_k_ff_1_qn, j_k_ff_2_qn, j_k_ff_3_qn, j_k_ff_4_qn;

  Clock CLOCK (.out(CLOCK_out));
  J_K_Flip_Flop j_k_ff_1 (.J(1'b1), .clk(CLOCK_out), .K(1'b1), .Q(out_5), .Qn(j_k_ff_1_qn));  // open: preset, en, reset
  J_K_Flip_Flop j_k_ff_2 (
    .J(1'b1), .clk(j_k_ff_1_qn), .K(1'b1), .Q(out_4), .Qn(j_k_ff_2_qn));  // open: preset, en, reset
  // Probe on {out_1, out_2, out_3, out_4, out_5}
  J_K_Flip_Flop j_k_ff_3 (
    .J(1'b1), .clk(j_k_ff_2_qn), .K(1'b1), .Q(out_3), .Qn(j_k_ff_3_qn));  // open: preset, en, reset
  J_K_Flip_Flop j_k_ff_4 (
    .J(1'b1), .clk(j_k_ff_3_qn), .K(1'b1), .Q(out_2), .Qn(j_k_ff_4_qn));  // open: preset, en, reset
  J_K_Flip_Flop j_k_ff_5 (.J(1'b1), .clk(j_k_ff_4_qn), .K(1'b1), .Q(out_1));  // open: Qn, preset, en, reset
endmodule

module DOWN (
  output out_1,
  output out_2,
  output out_3,
  output out_4
);

  wire CLOCK_out;

  Clock CLOCK (.out(CLOCK_out));
  J_K_Flip_Flop j_k_ff_1 (.J(1'b1), .clk(CLOCK_out), .K(1'b1), .Q(out_4));  // open: Qn, preset, en, reset
  J_K_Flip_Flop j_k_ff_2 (.J(1'b1), .clk(out_4), .K(1'b1), .Q(out_3));  // open: Qn, preset, en, reset
  // Probe on {out_1, out_2, out_3, out_4}
  J_K_Flip_Flop j_k_ff_3 (.J(1'b1), .clk(out_3), .K(1'b1), .Q(out_2));  // open: Qn, preset, en, reset
  J_K_Flip_Flop j_k_ff_4 (.J(1'b1), .clk(out_2), .K(1'b1), .Q(out_1));  // open: Qn, preset, en, reset
endmodule

module SICRONO (
  output [2:0] out_1
);

  wire A_qn, and_1_out, C_qn, clock_1_out, or_1_out, or_2_out;

  Clock clock_1 (.out(clock_1_out));
  and and_1 (and_1_out, C_qn, out_1[1]);
  or or_1 (or_1_out, out_1[2], C_qn);
  J_K_Flip_Flop A (
    .J(and_1_out), .clk(clock_1_out), .K(and_1_out), .Q(out_1[2]), .Qn(A_qn));  // open: preset, en, reset
  // Probe on out_1
  J_K_Flip_Flop B (.J(or_1_out), .clk(clock_1_out), .K(or_1_out), .Q(out_1[1]));  // open: Qn, preset, en, reset
  or or_2 (or_2_out, out_1[1], A_qn);
  J_K_Flip_Flop C (.J(or_2_out), .clk(clock_1_out), .K(or_2_out), .Q(out_1[0]), .Qn(C_qn));  // open: preset, en, reset
endmodule
