// Logisim project CONTADOR UP.circ as structural Verilog: 1 circuit, main circuit main
module main (
  input  [4:0] in_1,
  output out_2,
  output out_3,
  output out_4,
  output out_5,
  output out_6
);

  wire CLOCK_out, j_k_ff_1_qn, j_k_ff_2_qn, j_k_ff_3_qn, j_k_ff_4_qn;

  Clock CLOCK (.out(CLOCK_out));
  J_K_Flip_Flop j_k_ff_1 (
    .J(1'b1), .clk(CLOCK_out), .K(1'b1), .Q(in_1[0]), .Qn(j_k_ff_1_qn));  // open: preset, en, reset
  J_K_Flip_Flop j_k_ff_2 (
    .J(1'b1), .clk(j_k_ff_1_qn), .K(1'b1), .Q(in_1[1]), .Qn(j_k_ff_2_qn));  // open: preset, en, reset
  J_K_Flip_Flop j_k_ff_3 (
    .J(1'b1), .clk(j_k_ff_2_qn), .K(1'b1), .Q(in_1[2]), .Qn(j_k_ff_3_qn));  // open: preset, en, reset
  J_K_Flip_Flop j_k_ff_4 (
    .J(1'b1), .clk(j_k_ff_3_qn), .K(1'b1), .Q(in_1[3]), .Qn(j_k_ff_4_qn));  // open: preset, en, reset
  J_K_Flip_Flop j_k_ff_5 (.J(1'b1), .clk(j_k_ff_4_qn), .K(1'b1), .Q(in_1[4]));  // open: Qn, preset, en, reset

  assign out_2 = in_1[4];
  assign out_3 = in_1[3];
  assign out_4 = in_1[2];
  assign out_5 = in_1[1];
  assign out_6 = in_1[0];
endmodule
